// Logisim project main_pomysly.circ as structural Verilog: 1 circuit, main circuit main
module main (
  input  [23:0] in_1,
  input  [23:0] in_2,
  input  [23:0] in_3,
  input  [23:0] in_4,
  input  [23:0] in_5,
  input  [23:0] in_6,
  input  [23:0] in_7,
  input  [23:0] in_8
);

  wire A, and_4_out, button_3_out, CLK_ANIM, CLK_IN, clock_1_out, comparator_1_eq, D, d_ff_1_q, d_ff_1_qn,
       Display_ready, Key_impulse, keyboard_1_avail, main_5_clk_out, main_6_clk_out, main_7_clk_out,
       main_8_clk_out, main_10_clk_timebar, Main_clk_out, not_1_out, not_2_out, or_1_out, or_2_out,
       pull_resistor_1_node, RESET, RstRgr, Scored, Start_Stop, TIMEOUT;
  wire [1:0] key;
  wire [2:0] and_2_out, and_3_out, bit_extender_1_out, bit_extender_2_out, bit_extender_3_out, Counter,
       divider_1_rem, Kolizja_tree, random_1_out, shift_register_1_out, SR1, SR2, SR3, SR4, SR5;
  wire [3:0] H1, H2, H3, H4;
  wire [6:0] keyboard_1_data;
  wire [13:0] Points_value;
  wire [23:0] main_4_o0, main_4_o1, main_4_o7, main_4_out_10, main_4_out_11, main_4_out_12, main_4_out_13,
       main_4_out_14, main_5_o0, main_5_o1, main_5_o2, main_5_o3, main_5_o4, main_5_o5, main_5_o6, main_5_o7,
       main_5_register_out, main_6_o0, main_6_o1, main_6_o2, main_6_o3, main_6_o4, main_6_o5, main_6_o6,
       main_6_o7, main_6_register_out, main_7_o0, main_7_o1, main_7_o2, main_7_o3, main_7_o4, main_7_o5,
       main_7_o6, main_7_o7, main_7_register_out, main_8_o0, main_8_o1, main_8_o2, main_8_o3, main_8_o4,
       main_8_o5, main_8_o6, main_8_o7, main_8_register_out, multiplexer_1_out, RegOut, ROM0, ROM1, ROM2,
       rom_1_data, rom_2_data;
  wire [31:0] Timer;

  Button button_1 (.out(RESET));
  Clock #(.highDuration(4), .lowDuration(4)) Animation_clk (.out(CLK_ANIM));
  Clock Main_clk (.out(Main_clk_out));
  D_Flip_Flop d_ff_1 (.clk(Start_Stop), .D(d_ff_1_qn), .Q(d_ff_1_q), .Qn(d_ff_1_qn));  // open: preset, en, reset
  and and_1 (CLK_IN, Main_clk_out, d_ff_1_q);
  Stop_countera_main main_1 (.Clk(CLK_ANIM), .Reset(Key_impulse), .Counter(Counter));
  assign bit_extender_1_out = {{2{D}}, D};  // Bit_Extender bit_extender_1
  assign bit_extender_2_out = {{2{A}}, A};  // Bit_Extender bit_extender_2
  assign and_2_out = Counter & bit_extender_1_out;  // AND_Gate and_2, 3 bits wide
  assign and_3_out = Counter & bit_extender_2_out;  // AND_Gate and_3, 3 bits wide
  ROM_Tree_main main_2 (.Counter(Counter), .ROM_0(ROM0), .ROM_1(ROM1), .ROM_2(ROM2));
  Clock clock_1 (.out(clock_1_out));
  ROM #(.addrWidth(3), .dataWidth(24)) rom_1 (.addr(and_2_out), .data(rom_1_data));  // open: sel
  ROM #(.addrWidth(3), .dataWidth(24)) rom_2 (.addr(and_3_out), .data(rom_2_data));  // open: sel
  Random #(.width(3)) random_1 (.clk(clock_1_out), .out(random_1_out));  // open: next, clr
  Multiplexer #(.select(2), .width(24)) multiplexer_1 (
    .in1(rom_1_data), .in2(rom_2_data), .out(multiplexer_1_out), .sel(key));  // open: in0, in3, en
  Divider #(.width(3)) divider_1 (.a(random_1_out), .b(3'b011), .rem(divider_1_rem));  // open: out, upper
  Shift_register_rom_control_main main_3 (
    .in_1(ROM0), .in_2(ROM1), .in_3(ROM2), .Output(RegOut), .Address(SR1));  // open: in_4, in_5, in_6, in_7, in_8
  Shift_Register #(.width(3), .length(5)) shift_register_1 (
    .in(divider_1_rem), .clk(Display_ready), .out(shift_register_1_out), .clr(RstRgr), .q0(SR1), .q1(SR2),
    .q2(SR3), .q3(SR4), .q4(SR5));  // open: shift, load, d0, d1, d2, d3, d4
  or or_1 (or_1_out, Key_impulse, RstRgr);
  Timberman_or_tree_disp_main main_4 (
    .in_3(Key_impulse), .Timber_in(multiplexer_1_out), .Counter(Counter), .O0(main_4_o0), .O1(main_4_o1),
    .out_10(main_4_out_10), .out_11(main_4_out_11), .out_12(main_4_out_12), .out_13(main_4_out_13),
    .out_14(main_4_out_14), .O7(main_4_o7), .Clk(main_8_clk_out), .Register_in(main_8_register_out),
    .Disp_ready(Display_ready), .in_4(or_1_out), .in_6(RstRgr));
  Shift_Register #(.width(3), .length(1)) shift_register_2 (
    .in(shift_register_1_out), .clk(Display_ready), .out(Kolizja_tree), .clr(Key_impulse));  // open: shift, load, d0, q0
  Screen_animation_segment_main main_5 (
    .Input_line(RegOut), .Impulse(Key_impulse), .Reset(RstRgr), .O0(main_5_o0), .O1(main_5_o1),
    .O2(main_5_o2), .Register_out(main_5_register_out), .O3(main_5_o3), .O4(main_5_o4), .O5(main_5_o5),
    .O6(main_5_o6), .O7(main_5_o7), .Clk_out(main_5_clk_out), .Clk(CLK_ANIM));
  DotMatrix #(.inputtype("row"), .matrixcols(24), .matrixrows(8)) dotmatrix_1 (
    .row0(main_5_o0), .row1(main_5_o1), .row2(main_5_o2), .row3(main_5_o3), .row4(main_5_o4),
    .row5(main_5_o5), .row6(main_5_o6), .row7(main_5_o7));
  Screen_animation_segment_main main_6 (
    .Input_line(main_5_register_out), .Impulse(Key_impulse), .Reset(RstRgr), .O0(main_6_o0), .O1(main_6_o1),
    .O2(main_6_o2), .Register_out(main_6_register_out), .O3(main_6_o3), .O4(main_6_o4), .O5(main_6_o5),
    .O6(main_6_o6), .O7(main_6_o7), .Clk_out(main_6_clk_out), .Clk(main_5_clk_out));
  DotMatrix #(.inputtype("row"), .matrixcols(24), .matrixrows(32)) dotmatrix_2 (
    .row0(main_6_o0), .row1(main_6_o1), .row2(main_6_o2), .row3(main_6_o3), .row4(main_6_o4),
    .row5(main_6_o5), .row6(main_6_o6), .row7(main_6_o7), .row8(main_7_o0), .row9(main_7_o1),
    .row10(main_7_o2), .row11(main_7_o3), .row12(main_7_o4), .row13(main_7_o5), .row14(main_7_o6),
    .row15(main_7_o7), .row16(main_8_o0), .row17(main_8_o1), .row18(main_8_o2), .row19(main_8_o3),
    .row20(main_8_o4), .row21(main_8_o5), .row22(main_8_o6), .row23(main_8_o7), .row24(main_4_o0),
    .row25(main_4_o1), .row26(main_4_out_10), .row27(main_4_out_11), .row28(main_4_out_12),
    .row29(main_4_out_13), .row30(main_4_out_14), .row31(main_4_o7));
  Screen_animation_segment_main main_7 (
    .Input_line(main_6_register_out), .Impulse(Key_impulse), .Reset(RstRgr), .O0(main_7_o0), .O1(main_7_o1),
    .O2(main_7_o2), .Register_out(main_7_register_out), .O3(main_7_o3), .O4(main_7_o4), .O5(main_7_o5),
    .O6(main_7_o6), .O7(main_7_o7), .Clk_out(main_7_clk_out), .Clk(main_6_clk_out));
  Screen_animation_segment_main main_8 (
    .Input_line(main_7_register_out), .Impulse(Key_impulse), .Reset(RstRgr), .O0(main_8_o0), .O1(main_8_o1),
    .O2(main_8_o2), .Register_out(main_8_register_out), .O3(main_8_o3), .O4(main_8_o4), .O5(main_8_o5),
    .O6(main_8_o6), .O7(main_8_o7), .Clk_out(main_8_clk_out), .Clk(main_7_clk_out));
  DotMatrix #(.matrixcols(32), .matrixrows(1)) dotmatrix_3 (
    .col0(Timer[31]), .col1(Timer[30]), .col2(Timer[29]), .col3(Timer[28]), .col4(Timer[27]),
    .col5(Timer[26]), .col6(Timer[25]), .col7(Timer[24]), .col8(Timer[23]), .col9(Timer[22]),
    .col10(Timer[21]), .col11(Timer[20]), .col12(Timer[19]), .col13(Timer[18]), .col14(Timer[17]),
    .col15(Timer[16]), .col16(Timer[15]), .col17(Timer[14]), .col18(Timer[13]), .col19(Timer[12]),
    .col20(Timer[11]), .col21(Timer[10]), .col22(Timer[9]), .col23(Timer[8]), .col24(Timer[7]),
    .col25(Timer[6]), .col26(Timer[5]), .col27(Timer[4]), .col28(Timer[3]), .col29(Timer[2]),
    .col30(Timer[1]), .col31(Timer[0]));
  or or_2 (or_2_out, RESET, RstRgr);
  not not_1 (not_1_out, Display_ready);
  Hex_Digit_Display hex_digit_display_1 (.value(H3));  // open: dp
  Hex_Digit_Display hex_digit_display_2 (.value(H4));  // open: dp
  Pull_Resistor pull_resistor_1 (.node(pull_resistor_1_node));
  Keyboard keyboard_1 (
    .clk(pull_resistor_1_node), .re(Display_ready), .clr(not_1_out), .avail(keyboard_1_avail),
    .data(keyboard_1_data));
  assign pull_resistor_1_node = keyboard_1_avail ? CLK_IN : 1'bz;  // Controlled_Buffer controlled_buffer_1
  // Probe on in_1
  // Probe on in_2
  // Probe on in_3
  // Probe on in_6
  Hex_Digit_Display hex_digit_display_3 (.value(H2));  // open: dp
  TIMEDISPLAY_main main_9 (
    .WHEN_1__SUB_TIME_ONE_TICK__WHEN_0_ADD_TIME_ON_TICK(Scored), .CLK(main_10_clk_timebar), .RESET(or_2_out),
    .OutputScreen(Timer), .TIME_OUT(TIMEOUT));
  Dynamic_difficulty_control_main main_10 (.Points_value(Points_value), .Clk_timebar(main_10_clk_timebar));
  DotMatrix #(.inputtype("row"), .matrixcols(24), .matrixrows(8)) dotmatrix_4 (
    .row0(in_1), .row1(in_2), .row2(in_3), .row3(in_6), .row4(in_4), .row5(in_7), .row6(in_5), .row7(in_8));
  Hex_Digit_Display hex_digit_display_4 (.value(H1));  // open: dp
  // Probe on in_4
  // Probe on in_7
  Button button_2 (.out(Start_Stop));
  PointCounter_main main_11 (
    .ADD(Scored), .RESET(RESET), .X000(H4), ._0X00(H3), ._00X0(H2), ._000X(H1), .Current_value(Points_value));  // open: LIMIT
  Key_recognition_main main_12 (
    .Keyboard_input(keyboard_1_data), .Out(key), .Clk(CLK_IN), .A(A), .D(D), .KeyImpulse(Key_impulse));
  // Probe on in_5
  // Probe on in_8
  assign bit_extender_3_out = {{1{1'b0}}, key};  // Bit_Extender bit_extender_3
  Comparator #(.width(3)) comparator_1 (
    .a(bit_extender_3_out), .b(Kolizja_tree), .eq(comparator_1_eq));  // open: gt, lt
  and and_4 (and_4_out, Display_ready, comparator_1_eq);
  Button button_3 (.out(button_3_out));
  not not_2 (not_2_out, comparator_1_eq);
  or or_3 (RstRgr, and_4_out, TIMEOUT, button_3_out);
  and and_5 (Scored, not_2_out, Display_ready);

  // Other names for the same wires on the sheet: _1[23:0] = in_1; _2[23:0] = in_2; _3[23:0] = in_3; _4[23:0] = in_6;
  //   _5[23:0] = in_4; _6[23:0] = in_7; _7[23:0] = in_5; _8[23:0] = in_8

  // Notes on the sheet:
  //   contents of rom_1 (hex, n*v repeats v):
  //   0 c cc de 7e 4e c 33
  //   contents of rom_2 (hex, n*v repeats v):
  //   0 300000 330000 7b0000 7e0000 720000 300000 cc0000
  //   //OBECNIE WSKAZNIK CZASU CIAGLE SIE RESETUJE
  //   //FINALNIE BEDZIE PODPIETY DO START/STOP CALEJ GRY
endmodule
